# Fritzing sketch Board (saved by Fritzing 0.9.3b)
breadboards: 4

parts:
  Bauteil1 = Arduino Uno (Rev3)
  U1 = 74HC595 [package="DIP16 [THT]"]
  U2 = 74HC595 [package="DIP16 [THT]"]
  U3 = 74HC595 [package="DIP16 [THT]"]
  U4 = 74HC595 [package="DIP16 [THT]"]
  U5 = 74HC595 [package="DIP16 [THT]"]
  U6 = 74HC595 [package="DIP16 [THT]"]
  U7 = 74HC595 [package="DIP16 [THT]"]
  U8 = 74HC595 [package="DIP16 [THT]"]
  S2 = SWITCH-MOMENTARY-2 [package=reed_switch_plastic]
  S3 = SWITCH-MOMENTARY-2 [package=reed_switch_plastic]
  S4 = SWITCH-MOMENTARY-2 [package=reed_switch_plastic]
  S5 = SWITCH-MOMENTARY-2 [package=reed_switch_plastic]
  S6 = SWITCH-MOMENTARY-2 [package=reed_switch_plastic]
  S7 = SWITCH-MOMENTARY-2 [package=reed_switch_plastic]
  S8 = SWITCH-MOMENTARY-2 [package=reed_switch_plastic]
  S9 = SWITCH-MOMENTARY-2 [package=reed_switch_plastic]
  S10 = SWITCH-MOMENTARY-2 [package=reed_switch_plastic]
  S11 = SWITCH-MOMENTARY-2 [package=reed_switch_plastic]
  S12 = SWITCH-MOMENTARY-2 [package=reed_switch_plastic]
  S13 = SWITCH-MOMENTARY-2 [package=reed_switch_plastic]
  S17 = SWITCH-MOMENTARY-2 [package=reed_switch_plastic]
  S18 = SWITCH-MOMENTARY-2 [package=reed_switch_plastic]
  S19 = SWITCH-MOMENTARY-2 [package=reed_switch_plastic]
  S20 = SWITCH-MOMENTARY-2 [package=reed_switch_plastic]
  S21 = SWITCH-MOMENTARY-2 [package=reed_switch_plastic]
  S22 = SWITCH-MOMENTARY-2 [package=reed_switch_plastic]
  S23 = SWITCH-MOMENTARY-2 [package=reed_switch_plastic]
  S24 = SWITCH-MOMENTARY-2 [package=reed_switch_plastic]
  S25 = SWITCH-MOMENTARY-2 [package=reed_switch_plastic]
  S26 = SWITCH-MOMENTARY-2 [package=reed_switch_plastic]
  S27 = SWITCH-MOMENTARY-2 [package=reed_switch_plastic]
  S28 = SWITCH-MOMENTARY-2 [package=reed_switch_plastic]
  S29 = SWITCH-MOMENTARY-2 [package=reed_switch_plastic]
  S30 = SWITCH-MOMENTARY-2 [package=reed_switch_plastic]
  S31 = SWITCH-MOMENTARY-2 [package=reed_switch_plastic]
  S32 = SWITCH-MOMENTARY-2 [package=reed_switch_plastic]
  S33 = SWITCH-MOMENTARY-2 [package=reed_switch_plastic]
  S34 = SWITCH-MOMENTARY-2 [package=reed_switch_plastic]
  S35 = SWITCH-MOMENTARY-2 [package=reed_switch_plastic]
  S36 = SWITCH-MOMENTARY-2 [package=reed_switch_plastic]
  S37 = SWITCH-MOMENTARY-2 [package=reed_switch_plastic]
  S38 = SWITCH-MOMENTARY-2 [package=reed_switch_plastic]
  S39 = SWITCH-MOMENTARY-2 [package=reed_switch_plastic]
  S40 = SWITCH-MOMENTARY-2 [package=reed_switch_plastic]
  S41 = SWITCH-MOMENTARY-2 [package=reed_switch_plastic]
  S42 = SWITCH-MOMENTARY-2 [package=reed_switch_plastic]
  S43 = SWITCH-MOMENTARY-2 [package=reed_switch_plastic]
  S45 = SWITCH-MOMENTARY-2 [package=reed_switch_plastic]
  S46 = SWITCH-MOMENTARY-2 [package=reed_switch_plastic]
  S47 = SWITCH-MOMENTARY-2 [package=reed_switch_plastic]
  S48 = SWITCH-MOMENTARY-2 [package=reed_switch_plastic]
  S49 = SWITCH-MOMENTARY-2 [package=reed_switch_plastic]
  S51 = SWITCH-MOMENTARY-2 [package=reed_switch_plastic]
  S52 = SWITCH-MOMENTARY-2 [package=reed_switch_plastic]
  S53 = SWITCH-MOMENTARY-2 [package=reed_switch_plastic]
  S54 = SWITCH-MOMENTARY-2 [package=reed_switch_plastic]
  S55 = SWITCH-MOMENTARY-2 [package=reed_switch_plastic]
  S56 = SWITCH-MOMENTARY-2 [package=reed_switch_plastic]
  S57 = SWITCH-MOMENTARY-2 [package=reed_switch_plastic]
  S58 = SWITCH-MOMENTARY-2 [package=reed_switch_plastic]
  S59 = SWITCH-MOMENTARY-2 [package=reed_switch_plastic]
  S61 = SWITCH-MOMENTARY-2 [package=reed_switch_plastic]
  S62 = SWITCH-MOMENTARY-2 [package=reed_switch_plastic]
  S63 = SWITCH-MOMENTARY-2 [package=reed_switch_plastic]
  S64 = SWITCH-MOMENTARY-2 [package=reed_switch_plastic]
  S60 = SWITCH-MOMENTARY-2 [package=reed_switch_plastic]
  S44 = SWITCH-MOMENTARY-2 [package=reed_switch_plastic]
  S14 = SWITCH-MOMENTARY-2 [package=reed_switch_plastic]
  S15 = SWITCH-MOMENTARY-2 [package=reed_switch_plastic]
  S16 = SWITCH-MOMENTARY-2 [package=reed_switch_plastic]

nets:
  N1: Bauteil1.D8, U1.Q3
  N2: Bauteil1.D12/MISO, U1.Q7', U2.Q7', U3.Q7', U4.Q7', U5.Q7', U6.Q7', U7.Q7', U8.Q7'
  N3: Bauteil1.D13/SCK, U1.MR, U2.MR, U3.MR, U4.MR, U5.MR, U6.MR, U7.MR, U8.MR
  VCC: Bauteil1.5V, U1.VCC, U2.VCC, U3.VCC, U4.VCC, U5.VCC, U6.VCC, U7.VCC, U8.VCC, S2.2, S3.2, S4.2, S5.2, S6.2, S7.2, S8.2, S9.2, S10.2, S11.2, S12.2, S13.2, S17.2, S18.2, S19.2, S20.2, S21.2, S22.2, S23.2, S24.2, S25.2, S26.2, S27.2, S28.2, S29.2, S30.2, S31.2, S32.2, S14.2, S15.2, S16.2
  GND: Bauteil1.GND, U1.GND, U2.GND, U3.GND, U4.GND
  N4: U1.Q1, S8.1
  N5: U1.Q4, S4.1
  N6: U1.Q5, S3.1
  N7: U1.Q6, S2.1
  N8: U1.SH_CP, U2.Q3
  N9: U1.OE, S5.1
  N10: U1.DS, S6.1
  N11: U1.Q0, S7.1
  N12: U2.Q1, S16.1
  N13: U2.Q4, S12.1
  N14: U2.Q5, S11.1
  N15: U2.Q6, S10.1
  N16: U2.Q7, S9.1
  N17: U2.SH_CP, U3.Q3
  N18: U2.OE, S13.1
  N19: U2.DS, S14.1
  N20: U2.Q0, S15.1
  N21: U3.Q1, S24.1
  N22: U3.Q4, S20.1
  N23: U3.Q5, S19.1
  N24: U3.Q6, S18.1
  N25: U3.Q7, S17.1
  N26: U3.SH_CP, U4.Q3
  N27: U3.OE, S21.1
  N28: U3.DS, S22.1
  N29: U3.Q0, S23.1
  N30: U4.Q1, S32.1
  N31: U4.Q4, S28.1
  N32: U4.Q5, S27.1
  N33: U4.Q6, S26.1
  N34: U4.Q7, S25.1
  N35: U4.SH_CP, U6.Q3
  N36: U4.OE, S29.1
  N37: U4.DS, S30.1
  N38: U4.Q0, S31.1
  N39: U5.Q1, S34.1
  N40: U5.Q3, U6.SH_CP
  N41: U5.Q4, S48.1
  N42: U5.Q5, S41.1
  N43: U5.Q6, S42.1
  N44: U5.Q7, S58.1
  GND_2: U5.GND, U6.GND, U7.GND, U8.GND
  N45: U5.SH_CP, U7.Q3
  N46: U5.OE, S61.1
  N47: U5.DS, S44.1
  N48: U5.Q0, S60.1
  N49: U6.Q1, S49.1
  N50: U6.Q4, S38.1
  N51: U6.Q5, S47.1
  N52: U6.Q6, S63.1
  N53: U6.OE, S64.1
  N54: U6.DS, S54.1
  N55: U6.Q0, S37.1
  N56: U7.Q1, S57.1
  N57: U7.Q4, S52.1
  N58: U7.Q5, S33.1
  N59: U7.Q6, S35.1
  N60: U7.Q7, S53.1
  N61: U7.SH_CP, U8.Q3
  N62: U7.OE, S59.1
  N63: U7.DS, S40.1
  N64: U7.Q0, S39.1
  N65: U8.Q1, S43.1
  N66: U8.Q4, S56.1
  N67: U8.Q5, S62.1
  N68: U8.Q6, S51.1
  N69: U8.Q7, S36.1
  N70: U8.OE, S45.1
  N71: U8.DS, S46.1
  N72: U8.Q0, S55.1
  N73: S33.2, S34.2, S35.2, S36.2, S37.2, S38.2, S39.2, S40.2, S41.2, S42.2, S43.2, S45.2, S46.2, S47.2, S48.2, S49.2, S51.2, S52.2, S53.2, S54.2, S55.2, S56.2, S57.2, S58.2, S59.2, S61.2, S62.2, S63.2, S64.2, S60.2, S44.2

notes:
  Die shift Register sind CD4021BE
  Grün -> Latch Pin
  Schwarz -> Clock Pin
  Weiß -> Data Pin
